# Fritzing sketch bulb-boy-1 (saved by Fritzing 0.9.3b)
circuit board: 6.88566cm x 5.36311cm
breadboards: 1

parts:
  BULB_BOY_1 = Arduino Uno (Rev3)
  R1 = Resistor [tolerance=±5% resistance=10k package=THT]
  OPTO = 6n137 Optocoupler [part_number=6N137 package="DIP (Dual Inline) [THT]"]
  MIDI = DIN-5 jack (MIDI) [package=THT]
  R2 = Resistor [tolerance=±5% resistance=4.7k package=THT]
  R3 = Resistor [tolerance=±5% resistance=220 package=THT]
  D1 = Rectifier Diode [part_number=1N914 package="300 mil [THT]"]
  R4 = Resistor [tolerance=±5% resistance=220 package=THT]
  SSR5 = Molex Picoblade Series Header [part_number=0533980271 package=Picoblade-53398-0271]
  SSR1 = Molex Picoblade Series Header [part_number=0533980271 package=Picoblade-53398-0271]
  SSR4 = Molex Picoblade Series Header [part_number=0533980271 package=Picoblade-53398-0271]
  SSR2 = Molex Picoblade Series Header [part_number=0533980271 package=Picoblade-53398-0271]
  SSR3 = Molex Picoblade Series Header [part_number=0533980271 package=Picoblade-53398-0271]
  ZERO = Molex Picoblade Series Header [part_number=0533980271 package=Picoblade-53398-0271]
  RUN/LOAD = Toggle Switch [package=THT]
  SSR6 = Molex Picoblade Series Header [part_number=0533980271 package=Picoblade-53398-0271]
  LCD = female pin header, 4 pins [form="♀ (female)"]

nets:
  N1: BULB_BOY_1.A4/SDA, LCD.pin3
  N2: BULB_BOY_1.A5/SCL, LCD.pin4
  N3: BULB_BOY_1.D8, SSR6.1
  GND: BULB_BOY_1.GND, OPTO.GND, R2.Pin_0, SSR5.2, SSR1.2, SSR4.2, SSR2.2, SSR3.2, ZERO.2, SSR6.2, LCD.pin1
  N4: BULB_BOY_1.D0/RX, RUN/LOAD.COM
  N5: BULB_BOY_1.D2, R1.Pin_0, ZERO.1
  N6: BULB_BOY_1.D3_PWM, SSR1.1
  N7: BULB_BOY_1.D4, SSR2.1
  N8: BULB_BOY_1.D5_PWM, SSR3.1
  N9: BULB_BOY_1.D6_PWM, SSR4.1
  N10: BULB_BOY_1.D7, SSR5.1
  5V: BULB_BOY_1.5V, R1.Pin_1, OPTO.Vcc, R3.Pin_1, LCD.pin2
  N11: OPTO.Vf+, D1.cathode, R4.Pin_0
  N12: OPTO.Vf-, MIDI.5, D1.anode
  N13: OPTO.Vo, R3.Pin_0, RUN/LOAD.L2
  N14: OPTO.Ve, R2.Pin_1
  N15: MIDI.4, R4.Pin_1

custom parts:
  6n137 Optocoupler: 6n137 fast Optocoupler. With 8 pins on a 300mil dual inline package (DIP) footprint. Ve is strobe input. Output is inverting.
