# Fritzing sketch shield-sketch-relayout (saved by Fritzing 0.9.3b)
circuit board: 6.88566cm x 5.36311cm
breadboards: 1

parts:
  BULB_BOY_1 = Arduino Uno (Rev3)
  R1 = Resistor [tolerance=±5% resistance=10k package=THT]
  OPTO = 6n137 Optocoupler [part_number=6N137 package="DIP (Dual Inline) [THT]"]
  MIDI = DIN-5 jack (MIDI) [package=THT]
  R2 = Resistor [tolerance=±5% resistance=4.7k package=THT]
  R3 = Resistor [tolerance=±5% resistance=220 package=THT]
  D1 = Rectifier Diode [part_number=1N914 package="300 mil [THT]"]
  R4 = Resistor [tolerance=±5% resistance=220 package=THT]
  RUN/LOAD = Toggle Switch [package=THT]
  SSR2 = Header 2 [package=jst-2-pth]
  SSR3 = Header 2 [package=jst-2-pth]
  SSR4 = Header 2 [package=jst-2-pth]
  SSR5 = Header 2 [package=jst-2-pth]
  SSR6 = Header 2 [package=jst-2-pth]
  SSR1 = Header 2 [package=jst-2-pth]
  ZERO = Header 2 [package=jst-2-pth]
  JP1 = Header 4 [package=jst-4-pth]

nets:
  N1: BULB_BOY_1.A4/SDA, JP1.2
  N2: BULB_BOY_1.A5/SCL, JP1.1
  N3: BULB_BOY_1.D8, SSR6.2
  GND: BULB_BOY_1.GND, OPTO.GND, R2.Pin_0, SSR2.1, SSR3.1, SSR4.1, SSR5.1, SSR6.1, SSR1.1, ZERO.1, JP1.4
  N4: BULB_BOY_1.D0/RX, RUN/LOAD.COM
  N5: BULB_BOY_1.D2, R1.Pin_0, ZERO.2
  N6: BULB_BOY_1.D3_PWM, SSR1.2
  N7: BULB_BOY_1.D4, SSR2.2
  N8: BULB_BOY_1.D5_PWM, SSR3.2
  N9: BULB_BOY_1.D6_PWM, SSR4.2
  N10: BULB_BOY_1.D7, SSR5.2
  5V: BULB_BOY_1.5V, R1.Pin_1, OPTO.Vcc, R3.Pin_1, JP1.3
  N11: OPTO.Vf+, D1.cathode, R4.Pin_0
  N12: OPTO.Vf-, MIDI.5, D1.anode
  N13: OPTO.Vo, R3.Pin_0, RUN/LOAD.L2
  N14: OPTO.Ve, R2.Pin_1
  N15: MIDI.4, R4.Pin_1

custom parts:
  6n137 Optocoupler: 6n137 fast Optocoupler. With 8 pins on a 300mil dual inline package (DIP) footprint. Ve is strobe input. Output is inverting.
