# Fritzing sketch ssr-clone (saved by Fritzing 0.9.3b)
circuit board: 4.90127cm x 4.07341cm
breadboards: 1

parts:
  TRIAC = Basic FET P-Channel [package="TO220 [THT]"]
  LOAD = Header 3 [package=screwterminal-3.5mm-3_lock.007s]
  VAC = Header 3 [package=screwterminal-3.5mm-3_lock.007s]
  U2 = V18ZA2P [package=v18za2p]
  INPUT = Header 3 [package=screwterminal-3.5mm-3_lock.007s]
  OPTO = Optocoupler [package=THT]
  R3 = Resistor [tolerance=±5% resistance=270 package=THT]
  STATUS = smd LED [color="Red (633nm)" package="0603 [SMD]"]
  R1 = Resistor [tolerance=±5% resistance=510 package=THT]
  R2 = Resistor [tolerance=±5% resistance=100 package=THT]

nets:
  N1: TRIAC.gate, LOAD.1, U2.P$1
  N2: TRIAC.drain, VAC.1, R3.Pin_1
  N3: TRIAC.source, OPTO.Pin_6
  N4: LOAD.2, VAC.2, U2.P$2
  N5: LOAD.3, VAC.3, INPUT.3
  N6: INPUT.1, R1.Pin_0, R2.Pin_1
  N7: INPUT.2, OPTO.Pin_2, STATUS.cathode
  N8: OPTO.Pin_1, R1.Pin_1
  N9: OPTO.Pin_4, R3.Pin_0
  N10: STATUS.anode, R2.Pin_0
